// Logisim project alu.circ as structural Verilog: 3 circuits, main circuit main
module main (
  input  [31:0] X,
  input  [31:0] Y,
  input  [5:0] Switch__S,
  output Signed_Overflow,
  output [31:0] RESULT,
  output Equal
);

  wire adder_2_cout, and_2_out, Bit_0, Bit_1, comparator_1_gt, comparator_2_gt, multiplexer_1_out, nor_1_out,
       or_2_out, subtractor_1_bout;
  wire [3:0] adder_1_out, bit_extender_1_out, multiplier_1_out;
  wire [31:0] adder_2_out, and_1_out, bit_extender_2_out, bit_extender_3_out, bitpal_result, lfsr_result,
       or_1_out, shifter_1_out, shifter_2_out, shifter_3_out, subtractor_1_out;

  lfsr lfsr (.X(X), .Result(lfsr_result));
  nor nor_1 (nor_1_out, Switch__S[5], Switch__S[4]);
  assign bit_extender_1_out = {{3{1'b0}}, nor_1_out};  // Bit_Extender bit_extender_1
  assign or_1_out = X | Y;  // OR_Gate or_1, 32 bits wide
  bitpal bitpal (.X(X), .Result(bitpal_result));
  Multiplier #(.width(4)) multiplier_1 (
    .a(bit_extender_1_out), .b(4'b0110), .out(multiplier_1_out));  // open: cin, cout
  assign and_1_out = X & Y;  // AND_Gate and_1, 32 bits wide
  Adder #(.width(4)) adder_1 (
    .a(multiplier_1_out), .b(Switch__S[3:0]), .out({adder_1_out[3:2], Bit_0, adder_1_out[0]}));  // open: cin, cout
  Subtractor #(.width(32)) subtractor_1 (.a(X), .b(Y), .out(subtractor_1_out), .bout(subtractor_1_bout));  // open: bin
  Comparator #(.width(32), .mode("unsigned")) comparator_1 (
    .a(Y), .b(X), .gt(comparator_1_gt), .eq(Equal));  // open: lt
  Adder #(.width(32)) adder_2 (.a(X), .b(Y), .out(adder_2_out), .cout(adder_2_cout));  // open: cin
  Comparator #(.width(32)) comparator_2 (.a(Y), .b(X), .gt(comparator_2_gt));  // open: eq, lt
  Multiplexer #(.enable("false")) multiplexer_1 (
    .in0(adder_2_cout), .in1(subtractor_1_bout), .out(multiplexer_1_out), .sel(Bit_1));
  assign bit_extender_2_out = {{31{1'b0}}, comparator_2_gt};  // Bit_Extender bit_extender_2
  Shifter #(.width(32)) shifter_1 (.in(X), .\dist (Y[4:0]), .out(shifter_1_out));
  Shifter #(.width(32), .shift("lr")) shifter_2 (.in(X), .\dist (Y[4:0]), .out(shifter_2_out));
  Shifter #(.width(32), .shift("ar")) shifter_3 (.in(X), .\dist (Y[4:0]), .out(shifter_3_out));
  assign bit_extender_3_out = {{31{1'b0}}, comparator_1_gt};  // Bit_Extender bit_extender_3
  or or_2 (or_2_out, adder_1_out[0], adder_1_out[2]);
  or or_3 (Bit_1, or_2_out, adder_1_out[3]);
  and and_2 (and_2_out, multiplexer_1_out, ~Bit_1);  // AND_Gate
  Multiplexer #(.select(4), .width(32), .enable("false")) multiplexer_2 (
    .in0(adder_2_out), .in1(adder_2_out), .in2(subtractor_1_out), .in3(subtractor_1_out), .in4(and_1_out),
    .in5(or_1_out), .in6(shifter_1_out), .in8(shifter_2_out), .in9(shifter_3_out), .in10(bit_extender_2_out),
    .in11(bit_extender_3_out), .in14(bitpal_result), .in15(lfsr_result), .out(RESULT),
    .sel({adder_1_out[3:2], Bit_0, adder_1_out[0]}));  // open: in7, in12, in13
  and and_3 (Signed_Overflow, and_2_out, ~Bit_0);  // AND_Gate

  // Notes on the sheet:
  //   INPUTS to your circuit
  //   INPUT to your circuit
endmodule

module bitpal (
  input  [31:0] X,
  output [31:0] Result
);

  wire nor_1_out, xor_1_out, xor_2_out, xor_3_out, xor_4_out, xor_5_out, xor_6_out, xor_7_out, xor_8_out,
       xor_9_out, xor_10_out, xor_11_out, xor_12_out, xor_13_out, xor_14_out, xor_15_out, xor_16_out;

  xor xor_1 (xor_1_out, X[15], X[16]);
  xor xor_2 (xor_2_out, X[14], X[17]);
  xor xor_3 (xor_3_out, X[13], X[18]);
  xor xor_4 (xor_4_out, X[12], X[19]);
  xor xor_5 (xor_5_out, X[11], X[20]);
  xor xor_6 (xor_6_out, X[10], X[21]);
  xor xor_7 (xor_7_out, X[9], X[22]);
  xor xor_8 (xor_8_out, X[8], X[23]);
  xor xor_9 (xor_9_out, X[7], X[24]);
  xor xor_10 (xor_10_out, X[6], X[25]);
  xor xor_11 (xor_11_out, X[5], X[26]);
  xor xor_12 (xor_12_out, X[4], X[27]);
  xor xor_13 (xor_13_out, X[3], X[28]);
  xor xor_14 (xor_14_out, X[2], X[29]);
  xor xor_15 (xor_15_out, X[1], X[30]);
  xor xor_16 (xor_16_out, X[0], X[31]);
  nor nor_1 (nor_1_out, xor_1_out, xor_2_out, xor_3_out, xor_4_out, xor_5_out, xor_6_out, xor_7_out, xor_8_out, xor_9_out, xor_10_out, xor_11_out, xor_12_out, xor_13_out, xor_14_out, xor_15_out, xor_16_out);
  assign Result = {{31{1'b0}}, nor_1_out};  // Bit_Extender bit_extender_1
endmodule

module lfsr (
  input  [31:0] X,
  output [31:0] Result
);

  wire xor_1_out, xor_2_out, xor_3_out;
  wire [31:0] bit_extender_1_out, shifter_1_out, shifter_2_out;

  xor xor_1 (xor_1_out, X[0], X[2]);
  xor xor_2 (xor_2_out, xor_1_out, X[6]);
  Shifter #(.width(32), .shift("lr")) shifter_1 (.in(X), .\dist (5'b00001), .out(shifter_1_out));
  xor xor_3 (xor_3_out, xor_2_out, X[7]);
  assign Result = shifter_2_out | shifter_1_out;  // OR_Gate or_1, 32 bits wide
  assign bit_extender_1_out = {{31{1'b0}}, xor_3_out};  // Bit_Extender bit_extender_1
  Shifter #(.width(32)) shifter_2 (.in(bit_extender_1_out), .\dist ({5{1'b1}}), .out(shifter_2_out));
endmodule
