// Logisim project cpu.circ as structural Verilog: 3 circuits, main circuit main
module main (
  input  [31:0] RS_READ_VALUE,
  input  [31:0] RT_READ_VALUE,
  input  [31:0] INSTRUCTION,
  input  CLOCK,
  input  RESET,
  output [31:0] t0,
  output [31:0] t1,
  output [31:0] t2,
  output [31:0] t3,
  output [4:0] RS,
  output [4:0] RT,
  output [4:0] Write_Register,
  output [31:0] RD_WRITE_VALUE,
  output RD_WRITE_ENABLE,
  output [23:0] FETCH_ADDRESS
);

  wire ALU_signed_overflow, and_2_out, and_3_out, comparator_1_eq, comparator_2_eq, comparator_3_gt,
       is_addiu, is_andi, is_beq, is_bne, is_j, is_jal, is_jr, is_jump, is_lb, is_lbu, is_lui, is_lw, is_ori,
       is_sb, is_sw, kill, multiplexer_11_out, or_1_out, or_2_out, rs_isin, rt_isin, rW_isin;
  wire [1:0] rs_in, rt_in, rW_in;
  wire [3:0] and_1_out;
  wire [4:0] multiplexer_13_out, rd, shamt;
  wire [5:0] funct, opcode;
  wire [15:0] immediate, multiplexer_9_out, multiplexer_10_out;
  wire [23:0] adder_1_out, adder_2_out, adder_4_out, EX_Fetch_Address, jump_addr, multiplexer_1_out,
       multiplexer_8_out, multiplexer_16_out, multiplexer_17_out, offset, subtractor_1_out, subtractor_2_out;
  wire [25:0] address;
  wire [31:0] adder_3_out, adder_5_out, ALUrst, and_4_out, bit_extender_1_out, bit_extender_3_out,
       bit_extender_4_out, bit_extender_5_out, bit_extender_6_out, bit_extender_7_out, bit_extender_8_out,
       bit_extender_9_out, bit_extender_10_out, MEM_out, multiplexer_2_out, multiplexer_3_out,
       multiplexer_6_out, multiplexer_7_out, multiplexer_12_out, multiplexer_19_out, multiplexer_20_out,
       multiplexer_21_out, multiplexer_22_out, multiplexer_23_out, multiplexer_24_out, or_5_out,
       register_2_q, rs_data, rs_in_data, rt_data, rt_in_data, shifter_1_out, shifter_2_out, Write_rt;

  assign bit_extender_1_out = {{27{1'b0}}, shamt};  // Bit_Extender bit_extender_1
  assign and_1_out = funct[5:2] & 4'b1111;  // AND_Gate and_1, 4 bits wide
  Multiplexer #(.width(24), .disabled(0), .enable("false")) multiplexer_1 (
    .in0(adder_2_out), .in1(jump_addr), .out(multiplexer_1_out), .sel(is_jump));
  Comparator #(.width(4)) comparator_1 (.a(4'b0000), .b(and_1_out), .eq(comparator_1_eq));  // open: gt, lt
  Register #(.width(24)) register_1 (.D(multiplexer_1_out), .Q(FETCH_ADDRESS), .clk(CLOCK));  // open: en, clr
  Multiplexer #(.width(32), .disabled(0), .enable("false")) multiplexer_2 (
    .in0(rs_data), .in1(rt_data), .out(multiplexer_2_out), .sel(comparator_1_eq));
  Multiplexer #(.width(32), .disabled(0), .enable("false")) multiplexer_3 (
    .in0(rt_data), .in1(rs_data), .out(multiplexer_3_out), .sel(comparator_1_eq));
  Multiplexer #(.width(32), .disabled(0), .enable("false")) multiplexer_4 (
    .in0(RS_READ_VALUE), .in1(rs_in_data), .out(rs_data), .sel(rs_isin));
  Multiplexer #(.width(32), .disabled(0), .enable("false")) multiplexer_5 (
    .in0(RT_READ_VALUE), .in1(rt_in_data), .out(rt_data), .sel(rt_isin));
  alu_main ALU (
    .Switch__S(funct), .X(multiplexer_2_out), .RESULT(ALUrst), .Signed_Overflow(ALU_signed_overflow),
    .Y(multiplexer_6_out));  // open: Equal
  Multiplexer #(.width(32), .disabled(0), .enable("false")) multiplexer_6 (
    .in0(multiplexer_3_out), .in1(bit_extender_1_out), .out(multiplexer_6_out), .sel(comparator_1_eq));
  Adder #(.width(24)) adder_1 (.a(EX_Fetch_Address), .b(offset), .out(adder_1_out));  // open: cin, cout
  LED led_1 (.in(ALU_signed_overflow));
  Multiplexer #(.width(32), .disabled(0), .enable("false")) multiplexer_7 (
    .in0(INSTRUCTION), .in1({32{1'b0}}), .out(multiplexer_7_out), .sel(kill));
  Adder #(.width(24)) adder_2 (.a(24'h1), .b(multiplexer_8_out), .out(adder_2_out));  // open: cin, cout
  Multiplexer #(.width(24), .disabled(0), .enable("false")) multiplexer_8 (
    .in0(FETCH_ADDRESS), .in1(adder_1_out), .out(multiplexer_8_out), .sel(kill));
  assign offset = {{8{multiplexer_10_out[15]}}, multiplexer_10_out};  // Bit_Extender bit_extender_2
  Register #(.width(32)) register_2 (.D(multiplexer_7_out), .Q(register_2_q), .clk(CLOCK));  // open: en, clr
  Register #(.width(24)) register_3 (.D(FETCH_ADDRESS), .Q(EX_Fetch_Address), .clk(CLOCK));  // open: en, clr
  Comparator #(.width(32)) comparator_2 (.a(rs_data), .b(rt_data), .eq(comparator_2_eq));  // open: gt, lt
  Multiplexer #(.width(16), .disabled(0), .enable("false")) multiplexer_9 (
    .in0({16{1'b0}}), .in1(immediate), .out(multiplexer_9_out), .sel(and_2_out));
  and and_2 (and_2_out, comparator_2_eq, is_beq);
  Multiplexer #(.width(16), .disabled(0), .enable("false")) multiplexer_10 (
    .in0(multiplexer_9_out), .in1(immediate), .out(multiplexer_10_out), .sel(and_3_out));
  and and_3 (and_3_out, ~comparator_2_eq, is_bne);  // AND_Gate
  regfile_main RegFile (
    .Read_register_1(rs_in), .Read_register_2(rt_in), .write_register(rW_in), .write_data(RD_WRITE_VALUE),
    .t0_Value(t0), .t1_Value(t1), .t2_Value(t2), .t3_Value(t3), .RegWrite(multiplexer_11_out), .clock(CLOCK),
    .Read_Data_1(rs_in_data), .Read_Data_2(rt_in_data));
  Multiplexer #(.disabled(0), .enable("false")) multiplexer_11 (
    .in0(1'b0), .in1(RD_WRITE_ENABLE), .out(multiplexer_11_out), .sel(rW_isin));
  inst ISA (
    .Instruction(register_2_q), .opcode(opcode), .immediate(immediate), .rt(RT), .rs(RS), .address(address),
    .funct(funct), .shamt(shamt), .rd(rd), .Write_REG(RD_WRITE_ENABLE));
  Adder #(.width(32)) adder_3 (.a(rs_data), .b(bit_extender_3_out), .out(adder_3_out));  // open: cin, cout
  assign bit_extender_3_out = {{16{immediate[15]}}, immediate};  // Bit_Extender bit_extender_3
  or or_1 (or_1_out, is_lbu, is_lb, is_sb);
  or or_2 (or_2_out, is_sb, is_sw);
  or or_3 (kill, is_jump, and_2_out, and_3_out);
  Comparator #(.width(6), .mode("unsigned")) comparator_3 (
    .a(6'b000100), .b(opcode), .gt(comparator_3_gt));  // open: eq, lt
  mem_main MEM (
    .Data_Mem_Addr(adder_3_out), .Data_Mem_In(rt_data), .ACCESS_BYTE(or_1_out), .MEM_WRITE(or_2_out),
    .CLOCK(CLOCK), .Data_Mem_Out(MEM_out));
  reg_selector is_inside (.Reg(RS), .r(rs_in), .is_inside(rs_isin));
  reg_selector is_inside_2 (.Reg(RT), .r(rt_in), .is_inside(rt_isin));
  reg_selector is_inside_3 (.Reg(Write_Register), .r(rW_in), .is_inside(rW_isin));
  Adder #(.width(24)) adder_4 (.a(FETCH_ADDRESS), .b(24'h1), .out(adder_4_out));  // open: cin, cout
  Multiplexer #(.width(32), .disabled(0), .enable("false")) multiplexer_12 (
    .in0(Write_rt), .in1(ALUrst), .out(multiplexer_12_out), .sel(comparator_3_gt));
  Multiplexer #(.width(5), .disabled(0), .enable("false")) multiplexer_13 (
    .in0(RT), .in1(rd), .out(multiplexer_13_out), .sel(comparator_3_gt));
  assign bit_extender_4_out = {{8{1'b0}}, adder_4_out};  // Bit_Extender bit_extender_4
  Multiplexer #(.width(32), .disabled(0), .enable("false")) multiplexer_14 (
    .in0(multiplexer_12_out), .in1(shifter_1_out), .out(RD_WRITE_VALUE), .sel(is_jal));
  Multiplexer #(.width(5), .disabled(0), .enable("false")) multiplexer_15 (
    .in0(multiplexer_13_out), .in1({5{1'b1}}), .out(Write_Register), .sel(is_jal));
  Subtractor #(.width(24)) subtractor_1 (.a(rs_data[23:0]), .b(24'h100000), .out(subtractor_1_out));  // open: bin, bout
  Subtractor #(.width(24)) subtractor_2 (.a(address[25:2]), .b(24'h100000), .out(subtractor_2_out));  // open: bin, bout
  or or_4 (is_jump, is_jr, is_jal, is_j);
  Shifter #(.width(32), .shift("lr")) shifter_1 (.in(bit_extender_4_out), .\dist (5'b01000), .out(shifter_1_out));
  Multiplexer #(.width(24), .disabled(0), .enable("false")) multiplexer_16 (
    .in0({24{1'b0}}), .in1(subtractor_1_out), .out(multiplexer_16_out), .sel(is_jr));
  Multiplexer #(.width(24), .disabled(0), .enable("false")) multiplexer_17 (
    .in0(multiplexer_16_out), .in1(subtractor_2_out), .out(multiplexer_17_out), .sel(is_jal));
  Multiplexer #(.width(24), .disabled(0), .enable("false")) multiplexer_18 (
    .in0(multiplexer_17_out), .in1(subtractor_2_out), .out(jump_addr), .sel(is_j));
  assign bit_extender_5_out = {{16{immediate[15]}}, immediate};  // Bit_Extender bit_extender_5
  assign bit_extender_6_out = {{16{1'b0}}, immediate};  // Bit_Extender bit_extender_6
  assign bit_extender_7_out = {{16{1'b0}}, immediate};  // Bit_Extender bit_extender_7
  assign bit_extender_8_out = {{16{1'b0}}, immediate};  // Bit_Extender bit_extender_8
  Comparator #(.width(6), .mode("unsigned")) comparator_4 (.a(opcode), .b(6'b001001), .eq(is_addiu));  // open: gt, lt
  Comparator #(.width(6), .mode("unsigned")) comparator_5 (.a(opcode), .b(6'b001000), .eq(is_andi));  // open: gt, lt
  Comparator #(.width(6), .mode("unsigned")) comparator_6 (.a(opcode), .b(6'b001101), .eq(is_ori));  // open: gt, lt
  Comparator #(.width(6), .mode("unsigned")) comparator_7 (.a(opcode), .b(6'b001111), .eq(is_lui));  // open: gt, lt
  Comparator #(.width(6), .mode("unsigned")) comparator_8 (.a(opcode), .b(6'b100000), .eq(is_lb));  // open: gt, lt
  Comparator #(.width(6), .mode("unsigned")) comparator_9 (.a(opcode), .b(6'b100100), .eq(is_lbu));  // open: gt, lt
  Comparator #(.width(6), .mode("unsigned")) comparator_10 (.a(opcode), .b(6'b100011), .eq(is_lw));  // open: gt, lt
  Comparator #(.width(6), .mode("unsigned")) comparator_11 (.a(opcode), .b(6'b101011), .eq(is_sw));  // open: gt, lt
  Comparator #(.width(6), .mode("unsigned")) comparator_12 (.a(opcode), .b(6'b101000), .eq(is_sb));  // open: gt, lt
  Comparator #(.width(6), .mode("unsigned")) comparator_13 (.a(opcode), .b(6'b000100), .eq(is_beq));  // open: gt, lt
  Comparator #(.width(6), .mode("unsigned")) comparator_14 (.a(opcode), .b(6'b000101), .eq(is_bne));  // open: gt, lt
  Comparator #(.width(6), .mode("unsigned")) comparator_15 (.a(opcode), .b(6'b000010), .eq(is_j));  // open: gt, lt
  Comparator #(.width(6), .mode("unsigned")) comparator_16 (.a(opcode), .b(6'b000011), .eq(is_jal));  // open: gt, lt
  Comparator #(.width(6), .mode("unsigned")) comparator_17 (.a(funct), .b(6'b001000), .eq(is_jr));  // open: gt, lt
  Multiplexer #(.width(32), .disabled(0), .enable("false")) multiplexer_19 (
    .in1(adder_5_out), .out(multiplexer_19_out), .sel(is_addiu));  // open: in0
  Adder #(.width(32)) adder_5 (.a(rs_data), .b(bit_extender_5_out), .out(adder_5_out));  // open: cin, cout
  Multiplexer #(.width(32), .disabled(0), .enable("false")) multiplexer_20 (
    .in0(multiplexer_19_out), .in1(or_5_out), .out(multiplexer_20_out), .sel(is_ori));
  assign or_5_out = rs_data | bit_extender_6_out;  // OR_Gate or_5, 32 bits wide
  Multiplexer #(.width(32), .disabled(0), .enable("false")) multiplexer_21 (
    .in0(multiplexer_20_out), .in1(shifter_2_out), .out(multiplexer_21_out), .sel(is_lui));
  Shifter #(.width(32)) shifter_2 (.in(bit_extender_7_out), .\dist (5'b10000), .out(shifter_2_out));
  Multiplexer #(.width(32), .disabled(0), .enable("false")) multiplexer_22 (
    .in0(multiplexer_21_out), .in1(and_4_out), .out(multiplexer_22_out), .sel(is_andi));
  assign and_4_out = bit_extender_8_out & rs_data;  // AND_Gate and_4, 32 bits wide
  Multiplexer #(.width(32), .disabled(0), .enable("false")) multiplexer_23 (
    .in0(multiplexer_22_out), .in1(MEM_out), .out(multiplexer_23_out), .sel(is_lw));
  Multiplexer #(.width(32), .disabled(0), .enable("false")) multiplexer_24 (
    .in0(multiplexer_23_out), .in1(bit_extender_9_out), .out(multiplexer_24_out), .sel(is_lb));
  assign bit_extender_9_out = {{24{MEM_out[7]}}, MEM_out[7:0]};  // Bit_Extender bit_extender_9
  Multiplexer #(.width(32), .disabled(0), .enable("false")) multiplexer_25 (
    .in0(multiplexer_24_out), .in1(bit_extender_10_out), .out(Write_rt), .sel(is_lbu));
  assign bit_extender_10_out = {{24{1'b0}}, MEM_out[7:0]};  // Bit_Extender bit_extender_10

  // Other names for the same wires on the sheet: rW[4:0] = Write_Register; WriteData[31:0] = RD_WRITE_VALUE;
  //   WriteReg = RD_WRITE_ENABLE

  // Notes on the sheet:
  //   These are outputs/inputs from run.circ
  //   These are outputs to run.circ
endmodule

module inst (
  input  [31:0] Instruction,
  output [5:0] opcode,
  output [15:0] immediate,
  output [25:0] address,
  output [5:0] funct,
  output [4:0] shamt,
  output [4:0] rd,
  output Write_REG,
  output [4:0] rt,
  output [4:0] rs
);

  wire and_1_out, comparator_1_eq, comparator_2_eq, comparator_3_eq, comparator_4_eq, comparator_5_eq,
       comparator_6_eq, comparator_7_eq, comparator_8_eq, or_1_out, or_2_out;
  wire [25:0] demultiplexer_2_out0;
  wire [25:16] demultiplexer_1_out0, demultiplexer_2_out1;

  Comparator #(.width(6), .mode("unsigned")) comparator_1 (
    .a(Instruction[31:26]), .b(6'b101000), .eq(comparator_1_eq));  // open: gt, lt
  Comparator #(.width(6), .mode("unsigned")) comparator_2 (
    .a(Instruction[31:26]), .b(6'b101011), .eq(comparator_2_eq));  // open: gt, lt
  Comparator #(.width(6), .mode("unsigned")) comparator_3 (
    .a(Instruction[31:26]), .b(6'b000100), .eq(comparator_3_eq));  // open: gt, lt
  Comparator #(.width(6), .mode("unsigned")) comparator_4 (
    .a(Instruction[31:26]), .b(6'b000101), .eq(comparator_4_eq));  // open: gt, lt
  Demultiplexer #(.width(26), .disabled(0), .enable("false")) demultiplexer_1 (
    .out0({demultiplexer_1_out0, immediate}), .out1(address), .in(demultiplexer_2_out0), .sel(or_2_out));
  Comparator #(.width(6), .mode("unsigned")) comparator_5 (
    .a(Instruction[31:26]), .b(6'b000010), .eq(comparator_5_eq));  // open: gt, lt
  Comparator #(.width(6), .mode("unsigned")) comparator_6 (
    .a(Instruction[31:26]), .b(6'b000011), .eq(comparator_6_eq));  // open: gt, lt
  Demultiplexer #(.width(26), .disabled(0), .enable("false")) demultiplexer_2 (
    .out0(demultiplexer_2_out0), .out1({demultiplexer_2_out1, rd, shamt, funct}), .in(Instruction[25:0]),
    .sel(comparator_7_eq));
  Comparator #(.width(6), .mode("unsigned")) comparator_7 (
    .a(Instruction[31:26]), .b({6{1'b0}}), .eq(comparator_7_eq));  // open: gt, lt
  or or_1 (or_1_out, comparator_1_eq, comparator_2_eq, comparator_3_eq, comparator_4_eq);
  or or_2 (or_2_out, comparator_5_eq, comparator_6_eq);
  Comparator #(.width(6), .mode("unsigned")) comparator_8 (
    .a(funct), .b(6'b001000), .eq(comparator_8_eq));  // open: gt, lt
  and and_1 (and_1_out, ~comparator_8_eq, comparator_7_eq);  // AND_Gate
  Multiplexer #(.width(5), .disabled(0), .enable("false")) multiplexer_1 (
    .in0(demultiplexer_1_out0[20:16]), .in1(demultiplexer_2_out1[20:16]), .out(rt), .sel(comparator_7_eq));
  Multiplexer #(.width(5), .disabled(0), .enable("false")) multiplexer_2 (
    .in0(demultiplexer_1_out0[25:21]), .in1(demultiplexer_2_out1[25:21]), .out(rs), .sel(comparator_7_eq));
  or or_3 (Write_REG, ~or_1_out, comparator_6_eq, and_1_out);  // OR_Gate

  assign opcode = Instruction[31:26];
endmodule

module reg_selector (
  input  [4:0] Reg,
  output [1:0] r,
  output is_inside
);

  wire comparator_1_gt, comparator_2_lt;
  wire [4:2] subtractor_1_out;

  Subtractor #(.width(5)) subtractor_1 (.a(Reg), .b(5'b01000), .out({subtractor_1_out, r}));  // open: bin, bout
  Comparator #(.width(5)) comparator_1 (.a(Reg), .b(5'b00111), .gt(comparator_1_gt));  // open: eq, lt
  Comparator #(.width(5)) comparator_2 (.a(Reg), .b(5'b01100), .lt(comparator_2_lt));  // open: gt, eq
  and and_1 (is_inside, comparator_1_gt, comparator_2_lt);
endmodule
