// Logisim project mem.circ as structural Verilog: 1 circuit, main circuit main
module main (
  input  [31:0] Data_Mem_Addr,
  input  [31:0] Data_Mem_In,
  input  ACCESS_BYTE,
  input  MEM_WRITE,
  input  CLOCK,
  output [31:0] Data_Mem_Out
);

  wire not_1_out;
  wire [7:0] multiplexer_1_out;
  wire [31:0] bit_extender_1_out;

  RAM #(.addrWidth(24), .dataWidth(32)) ram_1 (
    .addr(Data_Mem_Addr[25:2]), .data({Data_Mem_In[31:24], Data_Mem_In[31:24], Data_Mem_In[15:0]}),
    .sel(1'b1), .clk(CLOCK), .ld(not_1_out), .clr(1'b0));
  not not_1 (not_1_out, MEM_WRITE);
  assign bit_extender_1_out = {{24{1'b0}}, multiplexer_1_out};  // Bit_Extender bit_extender_1
  Multiplexer #(.select(2), .width(8), .disabled(0), .enable("false")) multiplexer_1 (
    .in0(Data_Mem_In[31:24]), .in1(Data_Mem_In[31:24]), .in2(Data_Mem_In[15:8]), .in3(Data_Mem_In[7:0]),
    .out(multiplexer_1_out), .sel(Data_Mem_Addr[1:0]));
  Multiplexer #(.width(32), .disabled(0), .enable("false")) multiplexer_2 (
    .in0({Data_Mem_In[31:24], Data_Mem_In[31:24], Data_Mem_In[15:0]}), .in1(bit_extender_1_out),
    .out(Data_Mem_Out), .sel(ACCESS_BYTE));

  assign Data_Mem_In[23:16] = Data_Mem_In[31:24];

  // Notes on the sheet:
  //   These are INPUTS to the circuit
  //   These are INPUTS to the circuit
  //   DO NOT CHANGE THE LOCATIONS OF THE INPUTS/OUTPUTS! IF YOU DO SO, YOU NEED TO MAKE SURE THE PINS ARE AT THE RIGHT PLACE!
  //   Yet again, the clock is not an actual clock, but an input, one that will be driven from a higher circuit
  //   This is an OUTPUT to the circuit
endmodule
